# Fritzing sketch 47seg (saved by Fritzing 0.9.3b)
breadboards: 1

parts:
  HS420561K1 = HS420561K [part_number=HS420561K package="DIP (Dual Inline) [THT]"]
  Part1 = BluePill
  R1 = Resistor [tolerance=±5% resistance=220 package=THT]
  R2 = Resistor [tolerance=±5% resistance=220 package=THT]
  R3 = Resistor [tolerance=±5% resistance=220 package=THT]
  R4 = Resistor [tolerance=±5% resistance=220 package=THT]
  S1 = Pushbutton [package="[THT]"]

nets:
  N1: HS420561K1.pin1, Part1.C14
  N2: HS420561K1.pin2, Part1.C13
  N3: HS420561K1.pin4, Part1.A0
  N4: HS420561K1.pin5, Part1.A1
  N5: HS420561K1.pin6, R4.Pin_1
  N6: HS420561K1.pin7, Part1.A5
  N7: HS420561K1.pin8, R3.Pin_1
  N8: HS420561K1.pin_9, R2.Pin_1
  N9: HS420561K1.pin_10, Part1.A6
  N10: HS420561K1.pin_11, Part1.B8
  N11: HS420561K1.pin_12, R1.Pin_1
  N12: Part1.B11, R4.Pin_0
  N13: Part1.GND2, S1.Pin_1, S1.Pin_2
  N14: Part1.B9, S1.Pin_3, S1.Pin_4
  N15: Part1.A9, R1.Pin_0
  N16: Part1.A8, R2.Pin_0
  N17: Part1.B15, R3.Pin_0
