# Fritzing sketch fingerprint (saved by Fritzing 0.9.3b)
breadboards: 1

parts:
  LCD1 = elegoo-2.8in-tft-display
  Mod1 = sensor_biometrico
  Part1 = BluePill

nets:
  N1: LCD1.LCD_D1, Part1.A1
  N2: LCD1.LCD_D0, Part1.A0
  N3: LCD1.LCD_D7, Part1.A7
  N4: LCD1.LCD_D6, Part1.A6
  N5: LCD1.LCD_D5, Part1.A5
  N6: LCD1.LCD_D4, Part1.A4
  N7: LCD1.LCD_D3, Part1.A3
  N8: LCD1.LCD_D2, Part1.A2
  N9: LCD1.LCD_RST, Part1.B7
  N10: LCD1.LCD_CS, Part1.B6
  N11: LCD1.LCD_RS, Part1.B5
  N12: LCD1.LCD_WR, Part1.B1
  N13: LCD1.LCD_RD, Part1.B0
  GND: LCD1.GND, Mod1.GND, Part1.GND3
  5V: LCD1.5V, Part1.5V
  N14: Mod1.VCC, Part1.3V31
  N15: Mod1.TX, Part1.B10
  N16: Mod1.RX, Part1.B11

custom parts:
  elegoo-2.8in-tft-display: 2.8 Inch TFT LCD Touch Screen with SD Card Socket. 240*320 pixels RGB. 4 chip white LED backlight.
  sensor_biometrico: Adafruit Optical Fingerprint Sensor
