# Fritzing sketch epaper_sketch (saved by Fritzing 0.9.3b)
breadboards: 1

parts:
  Part1 = BluePill
  Part2 = HC-05 [part_number=HC-05 package="breakout board"]
  Part3 = e-paper 1.54inch

nets:
  N1: Part1.A1, Part3.VCC
  N2: Part1.A3, Part3.DIN
  N3: Part1.A4, Part3.CLK
  N4: Part1.A5, Part3.CS
  N5: Part1.A7, Part3.DC
  3V3: Part1.3V3, Part2.VCC, Part3.BUSY
  N6: Part1.GND, Part3.RST
  GND2: Part1.GND2, Part2.GND
  N7: Part1.A10, Part2.RXD
  N8: Part1.A9, Part2.TXD
  N9: Part1.A2, Part3.GND

custom parts:
  HC-05: A commonly available HC-05 Bluetooth breakout board.
