# Fritzing sketch dino (saved by Fritzing 0.9.3b)
breadboards: 1

parts:
  Part1 = LCD1602-I2C
  Part2 = BluePill
  S1 = Pushbutton [package="[THT]"]

nets:
  GND: Part1.GND, Part2.GND3
  VCC: Part1.VCC, Part2.5V
  N1: Part1.SDA, Part2.B7
  N2: Part1.SCL, Part2.B6
  N3: Part2.B11, S1.Pin_1, S1.Pin_2
  N4: Part2.GND2, S1.Pin_3, S1.Pin_4

custom parts:
  LCD1602-I2C: A standard character display, usually with 2x16 characters. Comes in many colors with LCM1602 IIC attached.
