# Fritzing sketch lcdpara (saved by Fritzing 0.9.3b)
breadboards: 1

parts:
  Part1 = BluePill
  LCD1 = LCD screen

nets:
  N1: Part1.C13, LCD1.DB6
  N2: Part1.C14, LCD1.DB7
  N3: Part1.B0, LCD1.DB4
  N4: Part1.B10, LCD1.E
  N5: Part1.B11, LCD1.RS
  N6: Part1.3V3, LCD1.LED+
  N7: Part1.GND, LCD1.V0
  N8: Part1.GND2, LCD1.R/W, LCD1.LED-
  GND3: Part1.GND3, LCD1.VSS
  5V: Part1.5V, LCD1.VDD
  N9: Part1.B15, LCD1.DB3
  N10: Part1.B14, LCD1.DB2
  N11: Part1.B13, LCD1.DB1
  N12: Part1.B12, LCD1.DB0
  N13: Part1.B1, LCD1.DB5
