# Fritzing sketch pong (saved by Fritzing 0.9.3b)
breadboards: 1

parts:
  Part1 = BluePill
  M1 = MAX7219 8x8 single Led Matrix Module  # not connected
  RE2 = KY-040 Rotary encoder [package=THT]
  RE3 = KY-040 Rotary encoder [package=THT]

nets:
  N1: Part1.B0, RE2.CLK
  N2: Part1.B10, RE2.DT
  3V3: Part1.3V3, RE2.Vcc
  GND: Part1.GND, RE2.GND
  GND3: Part1.GND3, RE3.GND
  5V: Part1.5V, RE3.Vcc
  N3: Part1.B5, RE3.DT
  N4: Part1.B4, RE3.CLK
  N5: Part1.A15, RE3.SW
  N6: Part1.B1, RE2.SW

custom parts:
  MAX7219 8x8 single Led Matrix Module: Description: MAX7219 8x8 LedMatrix single Red Module Dimensions: 32x32mm Documents:
  KY-040 Rotary encoder: KY-040 Rotary Encoder with switch on breakout borad from AZ Delivery
