# Fritzing sketch temp (saved by Fritzing 0.9.3b)
breadboards: 1

parts:
  Part1 = BluePill
  Part2 = NeoPixel Stick [part_number=1426]
  DS1 = DS18B20 1-Wire Temperature Sensor [part_number=DS18B20]

nets:
  N1: Part1.A7, Part2.DATAIN
  3V3: Part1.3V3, DS1.VDD
  GND: Part1.GND, DS1.GND
  GND3: Part1.GND3, Part2.GND
  5V: Part1.5V, Part2.+5V
  N2: Part1.B3, DS1.DQ

custom parts:
  NeoPixel Stick: Make your own little LED strip arrangement with this stick of NeoPixel LEDs. We crammed 8 of the tiny 5050 (5mm x 5mm) smart RGB LEDs onto a PCB with mounting holes and a chainable design. Use only one microcontroller pin to control as many as you can chain together! Each LED is addressable as the driver chip is inside the LED. Each one has ~18mA constant current drive so the color will be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
