# Fritzing sketch sketch (saved by Fritzing 0.9.3b)
breadboards: 1

parts:
  DS1 = DS18B20 1-Wire Temperature Sensor [part_number=DS18B20]
  Part1 = BluePill
  ZS-042_RTC1 = ZS-042 RTC Module
  OLED_I2C1 = OLED 128x64 I2C Monochrome Display
  UNT = Pushbutton [package="[THT]"]
  PWR = Pushbutton [package="[THT]"]
  SHOW_DATE = Pushbutton [package="[THT]"]

nets:
  GND: DS1.GND, Part1.GND, OLED_I2C1.GND
  VDD: DS1.VDD, OLED_I2C1.VDD
  GND2: Part1.GND2, ZS-042_RTC1.GND
  N1: ZS-042_RTC1.SDA, OLED_I2C1.SDA
  N2: ZS-042_RTC1.SCL, OLED_I2C1.SCK
  N3: UNT.Pin_3, UNT.Pin_4, PWR.Pin_3, PWR.Pin_4, SHOW_DATE.Pin_3, SHOW_DATE.Pin_4
