# Fritzing sketch alarm (saved by Fritzing 0.9.3b)
breadboards: 1

parts:
  Part1 = BluePill
  Part2 = SPI OLED Monochrome 128x64 0.96 inch
  RE1 = KY-040 Rotary encoder [package=THT]
  S1 = Pushbutton [package="[THT]"]

nets:
  N1: Part1.C14, RE1.SW
  N2: Part1.C15, RE1.DT
  N3: Part1.A0, RE1.CLK
  N4: Part1.A7, Part2.SDA
  3V3: Part1.3V3, RE1.Vcc
  GND: Part1.GND, RE1.GND
  GND2: Part1.GND2, Part2.GND
  5V: Part1.5V, Part2.VDD
  N5: Part1.A11, S1.Pin_1, S1.Pin_2
  N6: Part1.B15, Part2.DC
  N7: Part1.B14, Part2.RES
  N8: Part1.B12, Part2.CS
  N9: S1.Pin_3, S1.Pin_4

custom parts:
  SPI OLED Monochrome 128x64 0.96 inch: Unknown 128x64 0.96 inch 128x64 SPI Monochrome OLED display
  KY-040 Rotary encoder: KY-040 Rotary Encoder with switch on breakout borad from AZ Delivery
